# Fritzing sketch Energy Monitor (saved by Fritzing 0.9.3b)
breadboards: 1

parts:
  MCU1 = Arduino Nano (Rev3.0)
  INA1 = INA219 High Side DC Current Sensor Breakout [part_number=904]
  J1_-_Input_power = Power Jack [package=power_jack_pth_lock]
  IC1_-_7805 = Voltage Regulator [package=78xxl]
  J2_-_Output_power = Power Jack [package=power_jack_pth_lock]

nets:
  GND: MCU1.GND, INA1.GND, J1_-_Input_power.GND, IC1_-_7805.GND, J2_-_Output_power.GND
  5V: MCU1.5V, INA1.VCC
  N1: MCU1.A5, INA1.SCL
  N2: MCU1.A4, INA1.SDA
  N3: INA1.VIN+, IC1_-_7805.OUT
  N4: INA1.VIN-, J2_-_Output_power.PWR
  N5: J1_-_Input_power.PWR, IC1_-_7805.IN

custom parts:
  INA219 High Side DC Current Sensor Breakout: This breakout board will solve all your power-monitoring problems. Instead of struggling with two multimeters, you can just use the handy INA219B chip on this breakout to both measure both the high side voltage and DC current draw over I2C with 1% precision. Most current-measuring devices such as our current panel meter are only good for low side measuring. That means that unless you want to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
